# Fritzing sketch slider (saved by Fritzing 0.9.3b)
circuit board: 13.0819cm x 8.137cm
breadboards: 1

parts:
  Arduino = Adafruit Metro Mini [part_number="Adafruit #2590"]
  R1 = Resistor [tolerance=±5% resistance=10k package=THT]
  R2 = Resistor [tolerance=±5% resistance=10k package=THT]
  R3 = Resistor [tolerance=±5% resistance=10k package=THT]
  R4 = Resistor [tolerance=±5% resistance=10k package=THT]
  R5 = Resistor [tolerance=±5% resistance=220k package=THT]
  R6 = Resistor [tolerance=±5% resistance=2.2k package=THT]
  Transoptor = Sharp PC847X [package=THT]
  R7 = Resistor [tolerance=±5% resistance=220 package=THT]
  R8 = Resistor [tolerance=±5% resistance=220 package=THT]
  Aparat = female pin header, 3 pins [form="♀ (female)"]
  Klawiatura = male pin header, 5 pins [form="♂ (male)"]
  Sterownik_silnika_krokowego = female pin header, 6 pins [form="♀ (female)"]
  LCD = LCD screen
  Pad1 = Pad [width=10.011487375768885 height=5.4828253500817974 connect=center]
  OUT- = female pin header, 1 pin [form="♀ (female)"]
  OUT+ = female pin header, 1 pin [form="♀ (female)"]
  IN+ = female pin header, 1 pin [form="♀ (female)"]
  IN- = female pin header, 1 pin [form="♀ (female)"]
  6-30V = Screw terminal - 2 pins [package=THT]

nets:
  N1: Arduino.AD4/SDA, Sterownik_silnika_krokowego.pin4
  N2: Arduino.AD3, Sterownik_silnika_krokowego.pin3
  N3: Arduino.AD2, Sterownik_silnika_krokowego.pin2
  N4: Arduino.AD1, Sterownik_silnika_krokowego.pin1
  N5: Arduino.IO13, R8.Pin_0
  N6: Arduino.IO12, R7.Pin_0
  N7: Arduino.IO11, LCD.RS
  N8: Arduino.IO10, LCD.E
  N9: Arduino.IO9, LCD.DB4
  N10: Arduino.IO8, LCD.DB5
  N11: Arduino.IO7, LCD.DB6
  N12: Arduino.IO6, LCD.DB7
  N13: Arduino.IO5, R1.Pin_1, Klawiatura.pin1
  N14: Arduino.IO4, R2.Pin_1, Klawiatura.pin2
  N15: Arduino.IO3, R3.Pin_1, Klawiatura.pin3
  N16: Arduino.IO2, R4.Pin_1, Klawiatura.pin4
  5V: Arduino.+5V, R5.Pin_1, Klawiatura.pin5, Sterownik_silnika_krokowego.pin6, LCD.VDD
  GND: Arduino.GND, R1.Pin_0, R2.Pin_0, R3.Pin_0, R4.Pin_0, R6.Pin_0, Transoptor.Pin_2, Transoptor.Pin_4, LCD.VSS, LCD.R/W, OUT-.pin1
  N17: Arduino.VIN, Pad1.pad, OUT+.pin1
  N18: R5.Pin_0, R6.Pin_1, LCD.V0
  N19: Transoptor.Pin_1, R7.Pin_1
  N20: Transoptor.Pin_3, R8.Pin_1
  N21: Transoptor.Pin_13, Aparat.pin3
  N22: Transoptor.Pin_14, Transoptor.Pin_16, Aparat.pin2
  N23: Transoptor.Pin_15, Aparat.pin1
  N24: IN+.pin1, 6-30V.pin2
  N25: IN-.pin1, 6-30V.pin1

notes:
  4x10kΩ
  +
  -
  OUT+
  Slider 0.2
  github.com/SebJez/slider

custom parts:
  Adafruit Metro Mini: We sure love the ATmega328 here at Adafruit, and we use them a lot for our own projects. The processor has plenty of GPIO, Analog inputs, hardware UART SPI and I2C, timers and PWM galore - just enough for most simple projects. When we need to go small, we use a Pro Trinket 3V or 5V, but if you want to have USB-to-Serial built in, we reach for an Adafruit METRO Mini. METRO Mini is the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
